// Logisim project ULA-cell.circ as structural Verilog
module ULA_cell (
  input  b,
  input  a,
  input  [2:0] OPcode,
  input  Vem1,
  output out_5,
  output Vai1
);

  wire adder_1_out, and_1_out, nand_1_out, not_1_out, or_1_out, undriven, undriven_2, undriven_3, xor_1_out;

  not not_1 (not_1_out, undriven_2);
  and and_1 (and_1_out, undriven_2, undriven);
  or or_1 (or_1_out, undriven_2, undriven);
  xor xor_1 (xor_1_out, undriven_2, undriven);
  nand nand_1 (nand_1_out, undriven_2, undriven);
  Adder #(.width(1)) adder_1 (.a(undriven_2), .b(undriven), .out(adder_1_out), .cin(undriven_3), .cout(Vai1));
  Multiplexer #(.select(3), .enable("false")) multiplexer_1 (
    .in0(and_1_out), .in1(or_1_out), .in2(xor_1_out), .in3(nand_1_out), .in4(not_1_out), .in7(adder_1_out),
    .out(out_5), .sel(OPcode));  // open: in5, in6
endmodule
